# Fritzing sketch ProyectoFritzing (saved by Fritzing 0.9.3b)
circuit board: 12.0421cm x 11.65cm
breadboards: 2

parts:
  SparkFun_ESP32_Thing_Plus1 = SparkFun ESP32 Thing Plus [part_number=14689]
  LED1 = RGB LED - (4 legs) [package="5 mm [THT]"]
  R1 = Resistor [tolerance=±5% resistance=220 package="2512 [SMD]"]
  LED2 = RGB LED - (4 legs) [package="5 mm [THT]"]
  R2 = Resistor [tolerance=±5% resistance=220 package="2512 [SMD]"]
  R3 = Resistor [tolerance=±5% resistance=220 package="2512 [SMD]"]
  R5 = Resistor [tolerance=±5% resistance=220 package="2512 [SMD]"]
  R6 = Resistor [tolerance=±5% resistance=220 package="2512 [SMD]"]
  T1 = LM35 Temperature Sensor [package="TO92 [THT]"]
  T2 = LM35 Temperature Sensor [package="TO92 [THT]"]
  D1 = P1000K [part_number=P1000K]
  U1 = Sharp PC817 [package=THT]
  M2 = DC Motor
  U2 = Sharp PC817 [package=THT]
  Componente1 = songle relay
  Componente2 = songle relay
  R7 = Resistor [tolerance=±5% resistance=100 package="0402 [SMD]"]
  R8 = Resistor [tolerance=±5% resistance=100 package="0402 [SMD]"]
  LED3 = smd LED [color="Red (633nm)" package="0603 [SMD]"]
  LED4 = smd LED [color="Red (633nm)" package="0603 [SMD]"]
  R9 = Resistor [tolerance=±5% resistance=1k package="0402 [SMD]"]
  Q1 = NPN-Transistor [package="TO92 [THT]"]
  Q2 = NPN-Transistor [package="TO92 [THT]"]
  R10 = Resistor [tolerance=±5% resistance=1k package="0402 [SMD]"]
  D2 = P1000K [part_number=P1000K]
  U3 = SWITCH_SPDT [package=kps-1290]
  U4 = SWITCH_SPDT [package=kps-1290]
  M1 = DC Motor
  J2 = Camdenboss CTB0158-2 [part_number=CTB0158-2 package=THT]
  J5 = Camdenboss CTB0158-2 [part_number=CTB0158-2 package=THT]
  R4 = Resistor [tolerance=±5% resistance=220 package="2512 [SMD]"]
  Componente4 = LCD1602-I2C  # not connected
  J1 = Camdenboss CTB0158-3 [part_number=CTB0158-3 package=THT]

nets (from the pcb view):
  N1: SparkFun_ESP32_Thing_Plus1.V_USB, T1.+Vs, T2.+Vs, D1.cathode, U1.Pin_4, U2.Pin_4, J1.pin3
  N2: SparkFun_ESP32_Thing_Plus1.12, R5.Pin_1
  N3: SparkFun_ESP32_Thing_Plus1.27, R1.Pin_1
  N4: SparkFun_ESP32_Thing_Plus1.15, R6.Pin_1
  N5: SparkFun_ESP32_Thing_Plus1.14, R4.Pin_1
  GND: SparkFun_ESP32_Thing_Plus1.GND, T1.GND, T2.GND, R7.Pin_0, R8.Pin_0, J1.pin1
  N6: SparkFun_ESP32_Thing_Plus1.A0, R2.Pin_1
  N7: SparkFun_ESP32_Thing_Plus1.A1, R3.Pin_1
  N8: SparkFun_ESP32_Thing_Plus1.A3, T2.Vout
  N9: SparkFun_ESP32_Thing_Plus1.A4, T1.Vout
  N10: SparkFun_ESP32_Thing_Plus1.MOSI, U4.S
  N11: SparkFun_ESP32_Thing_Plus1.17, J1.pin2
  N12: SparkFun_ESP32_Thing_Plus1.21, U3.S
  N13: LED1.red_cathode, R4.Pin_0
  GND_2: LED1.common_anode, LED2.common_anode, Componente1.GND, Componente2.GND, D2.cathode
  N14: LED1.green_cathode, R5.Pin_0
  N15: LED1.blue_cathode, R6.Pin_0
  N16: R1.Pin_0, LED2.red_cathode
  N17: LED2.green_cathode, R2.Pin_0
  N18: LED2.blue_cathode, R3.Pin_0
  N19: D1.anode, Componente1.VCC, Q1.C
  N20: U1.Pin_1, LED3.cathode
  N21: U1.Pin_2, R7.Pin_1
  N22: U1.Pin_3, R9.Pin_1
  N23: M2.pin_1, J5.pin2
  N24: M2.pin_2, Componente1.NO
  N25: U2.Pin_1, LED4.cathode
  N26: U2.Pin_2, R8.Pin_1
  N27: U2.Pin_3, R10.Pin_1
  N28: Componente1.COMMON, J5.pin1
  N29: Componente2.VCC, Q2.C, D2.anode
  N30: Componente2.NO, M1.pin_2
  N31: Componente2.COMMON, J2.pin2
  N32: LED3.anode, U3.P
  N33: LED4.anode, U4.P
  N34: R9.Pin_0, Q1.B
  N35: Q2.B, R10.Pin_0
  N36: M1.pin_1, J2.pin1

notes:
  110VAC
  9VDC
  Calentador de agua
  Oxigenador de agua

custom parts:
  SparkFun ESP32 Thing Plus: The SparkFun ESP32 Thing Plus enjoys all the amenities of the ESP32 Thing, but with a few added sparkles. We've lengthened the board just a bit to accommodate a Qwiic connector for all your Qwiic breakout needs. We've also moved a few pins around to make the board compatible with the Adafruit Huzzah32 – ESP32 Feather Board such that you can use all of those lovely shields available out there!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
  LCD1602-I2C: A standard character display, usually with 2x16 characters. Comes in many colors with LCM1602 IIC attached.
